// Logisim project 8bitsProcesador.circ as structural Verilog: 8 circuits, main circuit ALU
module main (
);

  wire ALU_zero, and_1_out, multiplexer_1_out, Relog_out, Unidad_de_control_alusrc, Unidad_de_control_branch,
       Unidad_de_control_jump, Unidad_de_control_memread, Unidad_de_control_memtoreg,
       Unidad_de_control_memwrite, Unidad_de_control_regdst, Unidad_de_control_regwrite;
  wire [1:0] \alucontrol_1_operación , Unidad_de_control_aluop;
  wire [7:0] adder_1_out, adder_2_out, ALU_alu_respuesta, bancoregistros_1_readdata1,
       bancoregistros_1_readdata2, bit_extender_1_out, IM_salida, multiplexer_2_out, multiplexer_3_out,
       multiplexer_4_out, multiplexer_5_out, PC_salida, ram_1_data, shifter_2_out;

  Clock Relog (.out(Relog_out));
  PC PC (.Entrada(multiplexer_4_out), .Relog(Relog_out), .Salida(PC_salida));  // open: Limpiar
  InstructionMemory IM (.Entrada(PC_salida), .Salida(IM_salida));
  Adder adder_1 (.a(PC_salida), .b(8'h1), .out(adder_1_out));  // open: cin, cout
  assign bit_extender_1_out = {{6{1'b0}}, IM_salida[1:0]};  // Bit_Extender bit_extender_1
  Shifter shifter_1 (.in(IM_salida), .\dist (3'b010), .out(adder_1_out));
  Multiplexer multiplexer_1 (
    .in0(IM_salida[3]), .in1(IM_salida[2]), .out(multiplexer_1_out), .sel(Unidad_de_control_regdst));  // open: en
  UnidadControl Unidad_de_control (
    .Entrada(IM_salida[7:5]), .RegDst(Unidad_de_control_regdst), .Branch(Unidad_de_control_branch),
    .MemRead(Unidad_de_control_memread), .MemtoReg(Unidad_de_control_memtoreg),
    .ALUOp(Unidad_de_control_aluop), .MemWrite(Unidad_de_control_memwrite),
    .ALUSrc(Unidad_de_control_alusrc), .RegWrite(Unidad_de_control_regwrite), .Jump(Unidad_de_control_jump));
  BancoRegistros bancoregistros_1 (
    .Leer_registro_0(IM_salida[4]), .Leer_registro_1(IM_salida[3]), .WriteRegister(multiplexer_1_out),
    .Write_data(multiplexer_5_out), .RegWrite(Unidad_de_control_regwrite), .Relog(Relog_out),
    .ReadData1(bancoregistros_1_readdata1), .ReadData2(bancoregistros_1_readdata2));
  Multiplexer #(.width(8)) multiplexer_2 (
    .in0(bancoregistros_1_readdata2), .in1(bit_extender_1_out), .out(multiplexer_2_out),
    .sel(Unidad_de_control_alusrc));  // open: en
  ALUControl alucontrol_1 (
    .\Función (IM_salida[1:0]), .ALUOp(Unidad_de_control_aluop), .\Operación (\alucontrol_1_operación ));
  Shifter shifter_2 (.in(bit_extender_1_out), .\dist (3'b010), .out(shifter_2_out));
  ALU ALU (
    .A(bancoregistros_1_readdata1), .B(multiplexer_2_out), .ALU_Opt(\alucontrol_1_operación ),
    .Zero(ALU_zero), .ALU_Respuesta(ALU_alu_respuesta));
  Adder adder_2 (.a(adder_1_out), .b(shifter_2_out), .out(adder_2_out));  // open: cin, cout
  and and_1 (and_1_out, Unidad_de_control_branch, ALU_zero);
  RAM #(.bus("separate")) ram_1 (
    .addr(ALU_alu_respuesta), .din(bancoregistros_1_readdata2), .data(ram_1_data),
    .str(Unidad_de_control_memwrite), .ld(Unidad_de_control_memread));  // open: sel, clk, clr
  Multiplexer #(.width(8)) multiplexer_3 (
    .in0(adder_1_out), .in1(adder_2_out), .out(multiplexer_3_out), .sel(and_1_out));  // open: en
  Multiplexer #(.width(8)) multiplexer_4 (
    .in0(multiplexer_3_out), .in1(adder_1_out), .out(multiplexer_4_out), .sel(Unidad_de_control_jump));  // open: en
  Multiplexer #(.width(8)) multiplexer_5 (
    .in0(bancoregistros_1_readdata2), .in1(ram_1_data), .out(multiplexer_5_out),
    .sel(Unidad_de_control_memtoreg));  // open: en
endmodule

module ALU (
  input  [7:0] A,
  input  [7:0] B,
  input  [1:0] ALU_Opt,
  output Zero,
  output [7:0] ALU_Respuesta
);

  wire [7:0] adder_1_out, and_1_out, or_1_out, subtractor_1_out;

  Adder adder_1 (.a(A), .b(B), .out(adder_1_out));  // open: cin, cout
  Subtractor subtractor_1 (.a(A), .b(B), .out(subtractor_1_out));  // open: bin, bout
  assign and_1_out = A & B;  // AND_Gate and_1, 8 bits wide
  assign or_1_out = A | B;  // OR_Gate or_1, 8 bits wide
  Multiplexer #(.select(2), .width(8)) multiplexer_1 (
    .in0(adder_1_out), .in1(subtractor_1_out), .in2(and_1_out), .in3(or_1_out), .out(ALU_Respuesta),
    .sel(ALU_Opt));  // open: en
  Comparator comparator_1 (.a({8{1'b0}}), .b(ALU_Respuesta), .eq(Zero));  // open: gt, lt
endmodule

// ALUCtrl
module ALUControl (
  input  [1:0] ALUOp,
  input  [1:0] \Función ,
  output [1:0] \Operación 
);

  wire and_1_out, not_1_out;

  not not_1 (not_1_out, ALUOp[0]);
  and and_1 (and_1_out, not_1_out, ALUOp[1]);
  Multiplexer multiplexer_1 (.in0(ALUOp[0]), .in1(\Función [0]), .out(\Operación [0]), .sel(and_1_out));  // open: en
  Multiplexer multiplexer_2 (.in0(ALUOp[1]), .in1(\Función [1]), .out(\Operación [1]), .sel(and_1_out));  // open: en
endmodule

module UnidadControl (
  input  [2:0] Entrada,
  output RegDst,
  output Branch,
  output MemRead,
  output MemtoReg,
  output [1:0] ALUOp,
  output MemWrite,
  output ALUSrc,
  output RegWrite,
  output Jump
);

  wire not_1_out, not_2_out, not_3_out, not_4_out, not_5_out, not_6_out, not_7_out, not_8_out, not_9_out,
       not_10_out;

  not not_1 (not_1_out, Entrada[0]);
  not not_2 (not_2_out, Entrada[1]);
  not not_3 (not_3_out, Entrada[2]);
  not not_4 (not_4_out, Entrada[1]);
  not not_5 (not_5_out, Entrada[2]);
  not not_6 (not_6_out, Entrada[0]);
  not not_7 (not_7_out, Entrada[2]);
  not not_8 (not_8_out, Entrada[2]);
  not not_9 (not_9_out, Entrada[0]);
  not not_10 (not_10_out, Entrada[1]);
  and R (ALUOp[1], not_1_out, not_2_out, not_3_out);
  and lw (MemRead, Entrada[0], not_4_out, not_5_out);
  and sw (MemWrite, not_6_out, Entrada[1], not_7_out);
  and beq (ALUOp[0], Entrada[0], Entrada[1], not_8_out);
  and j (Jump, not_9_out, not_10_out, Entrada[2]);
  or or_1 (ALUSrc, MemWrite, MemRead);
  or or_2 (RegWrite, MemRead, ALUOp[1]);

  assign Branch = ALUOp[0];
  assign MemtoReg = MemRead;
  assign RegDst = ALUOp[1];
endmodule

module PC (
  input  [7:0] Entrada,
  input  Limpiar,
  input  Relog,
  output [7:0] Salida
);

  Register register_1 (.D(Entrada), .Q(Salida), .clk(Relog), .clr(Limpiar));  // open: en
endmodule

// IM
module InstructionMemory (
  input  [7:0] Entrada,
  output [7:0] Salida
);

  RAM ram_1 (.addr(Entrada), .data(Salida));  // open: sel, clk, ld, clr
endmodule

// Banco de registros
module BancoRegistros (
  input  RegWrite,
  input  Leer_registro_0,
  input  Leer_registro_1,
  input  WriteRegister,
  input  [7:0] Write_data,
  input  Relog,
  output [7:0] ReadData1,
  output [7:0] ReadData2
);

  wire decoder_1_out0, decoder_1_out1;
  wire [7:0] register_1_q, register_2_q;

  Decoder decoder_1 (.out0(decoder_1_out0), .out1(decoder_1_out1), .sel(WriteRegister), .en(RegWrite));
  Register register_1 (.D(Write_data), .en(decoder_1_out0), .Q(register_1_q), .clk(Relog));  // open: clr
  Register register_2 (.D(Write_data), .en(decoder_1_out1), .Q(register_2_q), .clk(Relog));  // open: clr
  Multiplexer #(.width(8)) multiplexer_1 (
    .in0(register_1_q), .in1(register_2_q), .out(ReadData1), .sel(Leer_registro_0));  // open: en
  Multiplexer #(.width(8)) multiplexer_2 (
    .in0(register_1_q), .in1(register_2_q), .out(ReadData2), .sel(Leer_registro_1));  // open: en
endmodule

module load (
  input  Limpiar,
  input  in_2,
  output [1:0] out_3,
  output out_4,
  output out_5,
  output out_6,
  output [2:0] out_7
);

  wire alu_1_zero, and_1_out, multiplexer_1_out, unidadcontrol_1_alusrc, unidadcontrol_1_branch,
       unidadcontrol_1_jump, unidadcontrol_1_memread, unidadcontrol_1_memtoreg, unidadcontrol_1_memwrite,
       unidadcontrol_1_regdst, unidadcontrol_1_regwrite;
  wire [1:0] \alucontrol_1_operación , unidadcontrol_1_aluop;
  wire [6:0] bit_extender_1_out;
  wire [7:0] adder_1_out, adder_2_out, alu_1_alu_respuesta, bancoregistros_1_readdata1,
       bancoregistros_1_readdata2, bit_extender_2_out, multiplexer_2_out, multiplexer_3_out,
       multiplexer_4_out, multiplexer_5_out, pc_1_salida, ram_2_data, shifter_1_out;

  Clock clock_1 ();  // open: out
  PC pc_1 (.Entrada(multiplexer_4_out), .Relog(in_2), .Limpiar(Limpiar), .Salida(pc_1_salida));
  Adder adder_1 (.a(pc_1_salida), .b(8'h1), .out(adder_1_out));  // open: cin, cout
  RAM ram_1 (.addr(pc_1_salida), .data({out_7, out_6, out_5, out_4, out_3}));  // open: sel, clk, ld, clr
  assign bit_extender_1_out = {{2{1'b0}}, {out_6, out_5, out_4, out_3}};  // Bit_Extender bit_extender_1
  UnidadControl unidadcontrol_1 (
    .Entrada(out_7), .RegDst(unidadcontrol_1_regdst), .Branch(unidadcontrol_1_branch),
    .MemRead(unidadcontrol_1_memread), .MemtoReg(unidadcontrol_1_memtoreg), .ALUOp(unidadcontrol_1_aluop),
    .MemWrite(unidadcontrol_1_memwrite), .ALUSrc(unidadcontrol_1_alusrc),
    .RegWrite(unidadcontrol_1_regwrite), .Jump(unidadcontrol_1_jump));
  Multiplexer multiplexer_1 (
    .in0(out_5), .in1(out_6), .out(multiplexer_1_out), .sel(unidadcontrol_1_regdst));  // open: en
  assign bit_extender_2_out = {{6{1'b0}}, out_3};  // Bit_Extender bit_extender_2
  BancoRegistros bancoregistros_1 (
    .Leer_registro_0(out_6), .Leer_registro_1(out_5), .WriteRegister(multiplexer_1_out),
    .Write_data(multiplexer_5_out), .RegWrite(unidadcontrol_1_regwrite), .Relog(in_2),
    .ReadData1(bancoregistros_1_readdata1), .ReadData2(bancoregistros_1_readdata2));
  ALUControl alucontrol_1 (.\Función (out_3), .ALUOp(unidadcontrol_1_aluop), .\Operación (\alucontrol_1_operación ));
  Shifter shifter_1 (.in(bit_extender_2_out), .\dist (3'b010), .out(shifter_1_out));
  ALU alu_1 (
    .A(bancoregistros_1_readdata1), .B(multiplexer_2_out), .ALU_Opt(\alucontrol_1_operación ),
    .Zero(alu_1_zero), .ALU_Respuesta(alu_1_alu_respuesta));
  Multiplexer #(.width(8)) multiplexer_2 (
    .in0(bancoregistros_1_readdata2), .in1(bit_extender_2_out), .out(multiplexer_2_out),
    .sel(unidadcontrol_1_alusrc));  // open: en
  Adder adder_2 (.a(adder_1_out), .b(shifter_1_out), .out(adder_2_out));  // open: cin, cout
  Multiplexer #(.width(8)) multiplexer_3 (
    .in0(adder_1_out), .in1(adder_2_out), .out(multiplexer_3_out), .sel(and_1_out));  // open: en
  and and_1 (and_1_out, unidadcontrol_1_branch, alu_1_zero);
  RAM #(.bus("separate")) ram_2 (
    .addr(alu_1_alu_respuesta), .din(bancoregistros_1_readdata2), .data(ram_2_data),
    .str(unidadcontrol_1_memwrite), .clk(in_2), .ld(unidadcontrol_1_memread));  // open: sel, clr
  Multiplexer #(.width(8)) multiplexer_4 (
    .in0(multiplexer_3_out), .in1({adder_1_out[7], bit_extender_1_out}), .out(multiplexer_4_out),
    .sel(unidadcontrol_1_jump));  // open: en
  Multiplexer #(.width(8)) multiplexer_5 (
    .in0(alu_1_alu_respuesta), .in1(ram_2_data), .out(multiplexer_5_out), .sel(unidadcontrol_1_memtoreg));  // open: en
endmodule
